# Fritzing sketch SensoriamentoFirebase (saved by Fritzing 0.9.3b)
breadboards: 1

parts:
  U1 = NodeMCU V1.0
  RHT1 = Humidity and Temperature Sensor RHT03
  Componente1 = HC-SR501 Body Sensor Module
  R1 = Resistor [tolerance=±5% resistance=220 package="0402 [SMD]"]
  LED1 = smd LED [color="Green (555nm)" package="1206 [SMD]"]

nets:
  N1: U1.D3, R1.Pin_1
  GND: U1.GND, RHT1.GND_1, Componente1.GND, LED1.cathode
  N2: U1.D5, RHT1.Data-signal
  N3: U1.D6, Componente1.OUT
  VCC: U1.Vin, RHT1.Vcc, Componente1.VCC
  N4: R1.Pin_0, LED1.anode

custom parts:
  NodeMCU V1.0: ESP8266 based NodeMCU
  HC-SR501 Body Sensor Module: Pyroelectric Infrared PIR Motion Sensor Detector Module
